# Fritzing sketch Wiring (saved by Fritzing 1.0.1rc)
breadboards: 1

parts:
  M1 = JSN-SRO4T [package=THT]
  M2 = DOIT Esp32 DevKit v1 (30 pins long, 11 pins width) [part_number=ESP32S-PIN30]
  LED1 = RGB LED (com. cathode, rbg) [package="5 mm [THT]"]
  Part1 = LCD1602-I2C

nets:
  GND: M1.pin1, M2.GND, LED1.common_cathode, Part1.GND
  N1: M1.pin2, M2.D18
  N2: M1.pin3, M2.D19
  VIN: M1.pin4, M2.VIN, Part1.VCC
  N3: M2.D21, Part1.SDA
  N4: M2.D22, Part1.SCL
  N5: M2.D25, LED1.green_anode
  N6: M2.D26, LED1.blue_anode
  N7: M2.D27, LED1.red_anode

custom parts:
  JSN-SRO4T: JSN-SR04T Waterproof Ultrasonic Distance Measuring Module Integrated Ultrasonic Detection Module DC 5V.
  DOIT Esp32 DevKit v1 (30 pins long, 11 pins width): The DOIT Esp32 DevKit v1 is one of the development board created by DOIT to evaluate the ESP-WROOM-32 module. It is based on the ESP32 microcontroller that boasts Wifi, Bluetooth, Ethernet and Low Power support all in a single chip. (vanepp) made breadboard work, adjusted pin numbering and labels and reduced size of schematic and cleaned up pcb. This chip is 30pins long (2 x15) and 11 pins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
  LCD1602-I2C: A standard character display, usually with 2x16 characters. Comes in many colors with LCM1602 IIC attached.
